# Fritzing sketch Potentiometer (saved by Fritzing 0.7.12b)

parts:
  Arduino1 = Arduino
  R1 = Rotary Potentiometer (Large) [maximum_resistance=100kΩ package=THT]
  LED1 = smd LED [color="Red (633nm)" package="0805 [SMD]"]

nets:
  N1: Arduino1.GND, R1.leg2, LED1.cathode
  N2: Arduino1.D13, LED1.anode
  N3: Arduino1.+5V, R1.leg1
  N4: Arduino1.A2, R1.wiper
