# Fritzing sketch RHT03 (saved by Fritzing 0.7.12b)
breadboards: 1

parts:
  Arduino1 = Arduino
  RHT1 = Humidity and Temperature Sensor RHT03

nets:
  N1: Arduino1.D0RX, RHT1.Data-signal
  +5V: Arduino1.+5V, RHT1.Vcc
  N2: Arduino1.GND, RHT1.GND_2
